# Fritzing sketch schematic (saved by Fritzing 0.9.2b)
breadboards: 1

parts:
  RHT1 = Humidity and Temperature Sensor RHT03
  Part1 = Arduino Uno (Rev3)
  R1 = Resistor [tolerance=±5% resistance=10k package=THT]
  C1 = Ceramic Capacitor [capacitance=100nF package="100 mil [THT, multilayer]"]
  LCD1 = LCD screen

nets:
  VCC: RHT1.Vcc, Part1.5V, R1.Pin_1, C1.1, LCD1.LED+
  N1: RHT1.Data-signal, Part1.D4, R1.Pin_0
  N2: RHT1.GND_2, Part1.GND, C1.0, LCD1.LED-
  N3: Part1.A4/SDA, LCD1.DB6
  N4: Part1.A5/SCL, LCD1.DB7

notes:
  Vcc
  GND
